# Fritzing sketch ChristmasLightsWLED (saved by Fritzing 0.9.4)
circuit board: 8.53488cm x 5.63626cm
breadboards: 1

parts:
  IC1 = Voltage Regulator [part_number=LM7805 package=78xxl]
  C2 = Electrolytic Capacitor [capacitance=1µF voltage=50V package="100 mil [THT, electrolytic]"]
  S1 = Pushbutton [package="[THT]"]
  R1 = Resistor [tolerance=±5% resistance=10k package=THT]
  R2 = Resistor [tolerance=±5% resistance=470 package=THT]
  J1 = Camdenboss CTB0158-2 [part_number=CTB0158-2 package=THT]
  C4 = Capacitor Polarized [package=cpol-radial-100uf-25v]
  C3 = Capacitor Polarized [package=cpol-radial-100uf-25v]
  C5 = Capacitor Polarized [package=cpol-radial-100uf-25v]
  C1 = Electrolytic Capacitor [capacitance=470µF voltage=50V package="100 mil [THT, electrolytic]"]
  J2 = Camdenboss CTB0158-3 [part_number=CTB0158-3 package=THT]
  C6 = Capacitor [package=cap-pth-small-kit]
  D1 = Rectifier Diode [part_number=1N4001 package="300 mil [THT]"]
  ESP8266 = ESP8266 NodeMCU LoLin module

nets (from the pcb view):
  GND: IC1.GND, C2.-, S1.Pin_1, S1.Pin_2, J1.pin2, C4.-, C3.-, C5.-, C1.-, J2.pin2, C6.1, ESP8266.GND
  N1: IC1.IN, C1.+, D1.cathode
  N2: IC1.OUT, C2.+, R1.Pin_0, ESP8266.Vin
  N3: S1.Pin_3, S1.Pin_4, R1.Pin_1, ESP8266.D3
  N4: R2.Pin_0, ESP8266.D4
  N5: R2.Pin_1, J2.pin1
  N6: J1.pin1, C4.+, C3.+, C5.+, J2.pin3, C6.2, D1.anode

notes:
  12V
  5V
  WLED Board
  v0.1
  otherguy
  ⏚ 12V
  D ⏚ 12V

custom parts:
  ESP8266 NodeMCU LoLin module: ESP8266 based NodeMCU
